# Fritzing sketch Fritzing_Schematic (saved by Fritzing 0.9.0b)

parts:
  Part1 = Arduino Uno (Rev3)
  Part2 = Arduino Uno (Rev3)

nets:
  GND: Part1.GND, Part2.GND
  N1: Part1.D2, Part2.D3_PWM
  N2: Part1.D3_PWM, Part2.D2

notes:
  < FTDI
  IO >
